// Logisim project CustomMultiplier.circ as structural Verilog: 1 circuit, main circuit CustomMultiplier
module CustomMultiplier (
  input  [7:0] FirstOperand,
  input  [7:0] SecondOperand,
  input  Clock,
  input  in_4,
  input  in_5,
  input  in_6,
  input  in_7,
  input  in_8,
  input  in_9,
  output [7:0] Result,
  output Done
);

  wire and_1_out, and_2_out, B_clk, not_1_out, shift_register_1_p1, shift_register_1_p3, shift_register_1_p6,
       shift_register_3_p17, shift_register_3_p18, t_ff_1_q, t_ff_2_q;
  wire [7:0] register_1_q, register_2_q;

  T_Flip_Flop t_ff_1 (.T(in_4), .clk(Clock), .Q(t_ff_1_q));  // open: Qn, reset, preset
  Counter counter_1 ();  // open: clr, load, up, count, clk, D, carry, Q
  T_Flip_Flop t_ff_2 (.T(in_5), .clk(t_ff_1_q), .Q(t_ff_2_q));  // open: Qn, reset, preset
  Register register_1 (.D(FirstOperand), .clk(Clock), .Q(register_1_q));  // open: en, clr
  Register register_2 (.D(SecondOperand), .clk(B_clk), .Q(register_2_q));  // open: en, clr
  T_Flip_Flop t_ff_3 (.T(in_6), .clk(t_ff_2_q), .Q(B_clk));  // open: Qn, reset, preset
  and and_1 (and_1_out, register_1_q[0], register_2_q[0]);
  // Shift_Register shift_register_1: pin names not known; wires that end beside it: shift_register_1_p1, shift_register_1_p1, shift_register_1_p3, shift_register_1_p3, and_1_out, shift_register_1_p6, shift_register_1_p6
  and and_2 (and_2_out, B_clk, Clock);
  not not_1 (not_1_out, and_2_out);
  // Shift_Register shift_register_2: pin names not known; wires that end beside it: and_2_out, not_1_out, Clock, in_7, SecondOperand[0], SecondOperand[1], SecondOperand[2], SecondOperand[3]
  // Shift_Register shift_register_3: pin names not known; wires that end beside it: SecondOperand[4], SecondOperand[5], SecondOperand[6], SecondOperand[7], B_clk, in_8, B_clk, in_9, FirstOperand[0], FirstOperand[1], FirstOperand[2], FirstOperand[3], FirstOperand[4], FirstOperand[5], FirstOperand[6], FirstOperand[7], shift_register_3_p17, shift_register_3_p18, shift_register_3_p17, shift_register_3_p18
  // Pins of 1 and 8 bits meet at register_1_q
  // Pins of 1 and 8 bits meet at register_2_q

  // Other names for the same wires on the sheet: A[7:0] = FirstOperand; B[7:0] = SecondOperand; C[7:0] = Result;
  //   clk = Clock
endmodule
